# Fritzing sketch Covid Clock (saved by Fritzing 0.9.4)
breadboards: 1

parts:
  M1 = DOIT Esp32 DevKit v1 (30 pins long, 11 pins width) [part_number=ESP32S-PIN30]
  OLED1 = OLED 128x64 I2C Monochrome Display
  OLED2 = OLED 128x64 I2C Monochrome Display
  S1 = Pushbutton [package="[THT]"]
  R1 = Resistor [tolerance=±5% resistance=22k package="0603 [SMD]"]
  R2 = Resistor [tolerance=±5% resistance=82k package=THT]
  U2 = LIPO-1000mAh [package=lipo-1000]
  TP1 = TP4056 [chip_label=TP4056 package="DIP (Dual Inline) [THT]"]
  C2 = Ceramic Capacitor [capacitance=100nF voltage=16V package="100 mil [THT, multilayer]"]
  C1 = Electrolytic Capacitor [capacitance=0.1mF voltage=16V package="100 mil [THT, electrolytic]"]
  U3 = MPC1700 [package=sot23-3]

nets:
  VDD: M1.3V3, OLED1.VDD, OLED2.VDD, C2.0, C1.+, U3.OUT
  GND: M1.GND, M1.EN, OLED1.GND, OLED2.GND, S1.Pin_3, S1.Pin_4, R2.Pin_0, TP1.pin6, C2.1, C1.-, U3.GND
  N1: M1.D21, OLED1.SDA, OLED2.SDA
  N2: M1.D22, OLED1.SCK, OLED2.SCK
  N3: M1.D33, R1.Pin_0, R2.Pin_1
  N4: R1.Pin_1, TP1.pin3, U3.IN
  N5: U2.+, TP1.pin4
  N6: U2.-, TP1.pin5

custom parts:
  DOIT Esp32 DevKit v1 (30 pins long, 11 pins width): The DOIT Esp32 DevKit v1 is one of the development board created by DOIT to evaluate the ESP-WROOM-32 module. It is based on the ESP32 microcontroller that boasts Wifi, Bluetooth, Ethernet and Low Power support all in a single chip. (vanepp) made breadboard work, adjusted pin numbering and labels and reduced size of schematic and cleaned up pcb. This chip is 30pins long (2 x15) and 11 pins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
  TP4056: A DIP stand-in part for whatever IC you want. With 6 pins on a 300mil dual inline package (DIP) footprint.
  MPC1700: Small package LDO
